# Fritzing sketch robotic-arm-claw (saved by Fritzing 0.9.4)
breadboards: 1

parts:
  J1 = Basic Servo
  J2 = Basic Servo
  J3 = Basic Servo
  VCC1 = 4 x AAA Battery Mount
  Part1 = Arduino Uno (Rev3) - ICSP
  J4 = Basic Servo

nets:
  GND: J1.gnd, J2.gnd, J3.gnd, VCC1.-, Part1.GND, J4.gnd
  VCC: J1.vcc, J2.vcc, J3.vcc, VCC1.+, Part1.VIN, J4.vcc
  N1: J1.pulse, Part1.D6_PWM
  N2: J2.pulse, Part1.D5_PWM
  N3: J3.pulse, Part1.D4
  N4: Part1.D3_PWM, J4.pulse
